# Fritzing sketch shema_8x8 (saved by Fritzing 1.0.1rc)
breadboards: 2

parts:
  part = Arduino Uno (Rev3)
  Disp1 = 32mm 8x8 dot matrix column cathode led display with standard pcb pads
  R1 = Resistor [tolerance=±5% power=0.25 resistance=220 package=THT]
  R2 = Resistor [tolerance=±5% power=0.25 resistance=220 package=THT]
  R3 = Resistor [tolerance=±5% power=0.25 resistance=220 package=THT]
  R4 = Resistor [tolerance=±5% power=0.25 resistance=220 package=THT]
  R5 = Resistor [tolerance=±5% power=0.25 resistance=220 package=THT]
  R6 = Resistor [tolerance=±5% power=0.25 resistance=220 package=THT]
  R7 = Resistor [tolerance=±5% power=0.25 resistance=220 package=THT]
  R8 = Resistor [tolerance=±5% power=0.25 resistance=220 package=THT]
  S1 = Pushbutton [package="[THT]"]
  S2 = Pushbutton [package="[THT]"]
  R9 = Resistor [tolerance=±5% power=0.25 resistance=220 package=THT]
  R10 = Resistor [tolerance=±5% power=0.25 resistance=220 package=THT]

nets:
  N1: part.A0, S1.Pin_1, S1.Pin_2, R10.Pin_0
  N2: part.A1, S2.Pin_1, S2.Pin_2, R9.Pin_0
  N3: part.A2, R3.Pin_0
  N4: part.A3, R1.Pin_0
  N5: part.A4/SDA, R6.Pin_1
  N6: part.A5/SCL, R2.Pin_0
  N7: part.D9_PWM, Disp1.pin_13
  N8: part.D10_PWM/SS, R8.Pin_1
  N9: part.D11_PWM/MOSI, R5.Pin_1
  N10: part.D12/MISO, R7.Pin_1
  N11: part.D13/SCK, R4.Pin_1
  N12: part.D2, Disp1.pin_16
  N13: part.D3_PWM, Disp1.pin_15
  N14: part.D4, Disp1.pin_11
  N15: part.D6_PWM, Disp1.pin_10
  N16: part.5V, R9.Pin_1, R10.Pin_1
  N17: part.GND, S1.Pin_3, S1.Pin_4, S2.Pin_3, S2.Pin_4
  N18: Disp1.pin_9, R3.Pin_1
  N19: Disp1.pin_12, R2.Pin_1
  N20: Disp1.pin_14, R1.Pin_1
